# Fritzing sketch IoT_Schematic (saved by Fritzing 1.0.6)

parts:
  U1 = ESP32S-HiLetgo [part_number=ESP32S-HiLetgo]
  INA1 = INA219 DC Current Sensor Breakout
  SERVO1 = Tower Pro SG90 servo [part_number=101246]
  Grove1 = Grove OLED 128x96
  e-radionica_com1 = LM393 LDR breakout [part_number=100027]
  e-radionica_com2 = LM393 LDR breakout [part_number=100027]
  PV1 = Generic Small 6V Solar Panel  # not connected
  VCC1 = Battery
  TP1 = TP4056 [chip_label=TP4056 package="DIP (Dual Inline) [THT]"]

nets:
  N1: U1.GPIO34, e-radionica_com1.AO
  N2: U1.GPIO35, e-radionica_com2.AO
  GND: U1.GND, INA1.GND, SERVO1.GND, Grove1.GND, e-radionica_com1.GND, e-radionica_com2.GND, TP1.pin2
  VCC: U1.VIN, INA1.VCC, SERVO1.+5V, Grove1.VCC, e-radionica_com1.VCC, e-radionica_com2.VCC, TP1.pin1
  N3: U1.GPIO18, SERVO1.Signal
  N4: U1.GPIO21, INA1.SDA, Grove1.SDA
  N5: U1.GPIO22, INA1.SCL, Grove1.SCL
  N6: VCC1.-, TP1.pin5
  N7: VCC1.+, TP1.pin4

custom parts:
  ESP32S-HiLetgo: HiLetgo ESP-WROOM-32 ESP32 ESP-32S Development Board 2.4GHz Dual-Mode WiFi + Bluetooth Dual Cores Microcontroller The ESP32 integrated with Antenna switches, RF Balun, power amplifiers, low-noise amplifiers, filters, and management modules, and the entire solution occupies the least area of PCB. 2.4 GHz Wi-Fi plus Bluetooth dual-mode chip, with TSMC Ultra-low power consumption 40nm technology,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
  INA219 DC Current Sensor Breakout: INA DC Current Sensor Breakout
  Tower Pro SG90 servo: Original file by John De Cristofaro http://www.adafruit.com/products/1449 Adafruit Feedback Servo (Small) Edited by: e-radionica.com 28/9/2015
  Battery: Your standard 2x 18650 battery pack (7,4 Volts)
  TP4056: A DIP stand-in part for whatever IC you want. With 6 pins on a 300mil dual inline package (DIP) footprint.
